# Fritzing sketch FridaSchematics (saved by Fritzing 0.7.12b)
breadboards: 1

parts:
  Arduino1 = Arduino  # not connected
  Part1 = Arduino USB Host Shield
  Arduino_Ethernet_Shield1 = Arduino Ethernet Shield  # not connected
  R2 = Resistor [tolerance=±5% resistance=220 package=THT]
  J1 = Piezo Speaker  # not connected
  R3 = Photocell (LDR) [package=THT]  # not connected
  J2 = Screw terminal - 2 pins [package=THT]
  J3 = Screw terminal - 2 pins [package=THT]
  T1 = LM35 Temperature Sensor [package="TO92 [THT]"]  # not connected
  J4 = Screw terminal - 2 pins [package=THT]
  J5 = Screw terminal - 2 pins [package=THT]
  J6 = Screw terminal - 2 pins [package=THT]

nets:
  N1: Part1.5V-ARDUINO, J2.pin2, J4.pin1
  N2: Part1.A0, J6.pin1
  N3: Part1.A1, R2.Pin_1, J2.pin1
  N4: Part1.D3, J3.pin1
  N5: Part1.GND, R2.Pin_0, J3.pin2, J5.pin1

notes:
  I kjøleskapet
